# Fritzing sketch servo_circuit (saved by Fritzing 0.9.3b)
breadboards: 1

parts:
  Part1 = Arduino Due (Rev2b)
  J1 = Basic Servo
  J2 = Basic Servo
  VCC3 = Battery
  VCC4 = Battery
  VCC5 = Battery
  VCC6 = Battery

nets:
  GND: Part1.GND, J2.gnd, VCC4.-, VCC5.-
  N1: Part1.D2_PWM, J2.pulse
  N2: Part1.D3_PWM, J1.pulse
  VCC: J1.vcc, J2.vcc, VCC3.+, VCC6.+
